# Fritzing sketch porte_poulailler_wifi (saved by Fritzing 0.9.3b)

parts:
  Composant1 = Arduino Nano (Rev3.0)
  ZS-042_RTC1 = ZS-042 RTC Module
  S1 = H-Bridge with L298N
  M1 = DC Motor
  Power_plug1 = Power plug
  S4 = Toggle Switch [package=THT]
  U1 = AMS1117 step down module
  U2 = ESP8266 WiFi Module [part_number=ESP8266]

nets:
  N1: Composant1.D4, U2.GPIO_2
  N2: Composant1.D5, U2.GPIO_0
  N3: Composant1.D6, S4.L1
  N4: Composant1.D8, S1.IN2
  N5: Composant1.D9, S1.IN1
  N6: Composant1.D10, S1.ENA
  N7: Composant1.A5, ZS-042_RTC1.SCL
  N8: Composant1.A4, ZS-042_RTC1.SDA
  VCC: ZS-042_RTC1.VCC, S1.5V
  12V: S1.12V, Power_plug1.VCC
  GND: S1.GND, Power_plug1.GND, S4.COM
  N9: S1.M1-01, M1.pin_2
  N10: S1.M1-02, M1.pin_1
  N11: U1.GND-, U2.GND
  N12: U1.VOUT+, U2.VCC

notes:
  rtc
  alim 12V
  moteur
  ASM1117 converti 12v en 3v3
  ESP8266 flashé tasmota avec GPIO0 en relais ouverture (vert) et GPIO2 en relais fermeture (jaune)

custom parts:
  H-Bridge with L298N: h-bridge
  ESP8266 WiFi Module: Generic WiFi Module based on the ESP8266 with onboard PCB antenna and UART communications
